// Logisim project CS23B1067_Lab8.circ as structural Verilog: 1 circuit, main circuit main
module main (
  input  [1:0] S1S0,
  input  in_2,
  input  [3:0] I3I2I1I0,
  output [3:0] out_4
);

  wire clock_1_out, multiplexer_1_out, multiplexer_2_out, multiplexer_3_out, multiplexer_4_out;

  Clock clock_1 (.out(clock_1_out));
  D_Flip_Flop #(.trigger("falling")) d_ff_1 (
    .D(multiplexer_1_out), .clk(clock_1_out), .Q(out_4[3]));  // open: Qn, preset, reset
  Multiplexer #(.select(2)) multiplexer_1 (
    .in0(out_4[3]), .in1(in_2), .in2(out_4[2]), .in3(I3I2I1I0[3]), .out(multiplexer_1_out), .sel(S1S0));
  D_Flip_Flop #(.trigger("falling")) d_ff_2 (
    .D(multiplexer_2_out), .clk(clock_1_out), .Q(out_4[2]));  // open: Qn, preset, reset
  Multiplexer #(.select(2)) multiplexer_2 (
    .in0(out_4[2]), .in1(out_4[3]), .in2(out_4[1]), .in3(I3I2I1I0[2]), .out(multiplexer_2_out), .sel(S1S0));
  D_Flip_Flop #(.trigger("falling")) d_ff_3 (
    .D(multiplexer_3_out), .clk(clock_1_out), .Q(out_4[1]));  // open: Qn, preset, reset
  Multiplexer #(.select(2)) multiplexer_3 (
    .in0(out_4[1]), .in1(out_4[2]), .in2(out_4[0]), .in3(I3I2I1I0[1]), .out(multiplexer_3_out), .sel(S1S0));
  D_Flip_Flop #(.trigger("falling")) d_ff_4 (
    .D(multiplexer_4_out), .clk(clock_1_out), .Q(out_4[0]));  // open: Qn, preset, reset
  Multiplexer #(.select(2)) multiplexer_4 (
    .in0(out_4[0]), .in1(out_4[1]), .in2(in_2), .in3(I3I2I1I0[0]), .out(multiplexer_4_out), .sel(S1S0));
endmodule
